# Fritzing sketch VarispeedStepperCircuit (saved by Fritzing 0.9.3b)
breadboards: 1

parts:
  S1 = Toggle Switch [package=THT]
  R1 = Rotary Potentiometer (Small) [maximum_resistance=100kΩ package=THT]
  M1 = Stepper Motor - Bipolar
  Part1 = Arduino Uno (Rev3)
  PART1 = Big Easy Driver ROB-11876 [part_number=ROB-11876]

nets:
  N1: S1.COM, Part1.D2
  N2: S1.L2, R1.leg1, Part1.GND
  N3: R1.wiper, Part1.A0
  N4: R1.leg2, Part1.5V
  N5: M1.A, PART1.A#0
  N6: M1.C, PART1.A#1
  N7: M1.B, PART1.B#2
  N8: M1.D, PART1.B#3
  N9: Part1.D9_PWM, PART1.EN
  N10: Part1.D3_PWM, PART1.DR
  N11: Part1.D4, PART1.ST

notes:
  5V and Ground
  12V and Ground

custom parts:
  Big Easy Driver ROB-11876: The Big Easy Driver, designed by Brian Schmalz, is a stepper motor driver board for bi-polar stepper motors up to 1.4A/phase. It is based on the Allegro A4988 stepper driver chip. It’s the next version of the popular Easy Driver board. Each Big Easy Driver can drive up to about 1.4A per phase of a bi-polar stepper motor. It is a chopper microstepping driver which defaults to 16 step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
